# Fritzing sketch Top (saved by Fritzing 0.9.3b)
circuit board: 7.23695cm x 8.88573cm
breadboards: 1

parts:
  TO_BOTTOM = DB25M
  USB1 = USB Connectors [package=usb-a-s-nosilk]
  J = double row male pin header, 4 pins [form="♂ (male)"]
  TRS1 = Audio Jack (TRS) 3.5mm [package="4Ucon 08780 [THT]"]
  J_HOR = Basic Servo
  J_VER = Basic Servo
  CONN1 = shrouded pin header, 6 pins [form="♂ (shrouded male)"]

nets:
  GND: TO_BOTTOM.pin1, J_HOR.gnd, J_VER.gnd, CONN1.pin1
  N1: TO_BOTTOM.pin2, J_HOR.pulse
  N2: TO_BOTTOM.pin3, J_VER.pulse
  N3: TO_BOTTOM.pin4, CONN1.pin4
  N4: TO_BOTTOM.pin5, CONN1.pin3
  N5: TO_BOTTOM.pin6, J.pin1
  N6: TO_BOTTOM.pin7, J.pin4
  N7: TO_BOTTOM.pin8, TRS1.Ring
  N8: TO_BOTTOM.pin9, TRS1.Tip
  VCC: TO_BOTTOM.pin14, USB1.VBUS, J_HOR.vcc, J_VER.vcc, CONN1.pin6
  N9: TO_BOTTOM.pin15, CONN1.pin5
  N10: TO_BOTTOM.pin16, CONN1.pin2
  N11: USB1.D+, J.pin3
  N12: USB1.D-, J.pin2
  N13: USB1.GND, TRS1.Sleeve

notes:
  D+   D-
  Circuit V.0
  Top Robot
  0V 5V
  VIN 3V3
  SCL SDA
